# Fritzing sketch schets fritzing (saved by Fritzing 0.8.7b)
breadboards: 1

parts:
  Part1 = songle relay
  Q1 = NPN-Transistor [package="TO92 [THT]"]
  D1 = Rectifier Diode [part_number=1N4001 package="Melf DO-213 AB [SMD]"]
  DHT1 = DHT22 Humidity and Temperature Sensor
  LED1 = LED - 5mm [color="Red (633nm)" package="5 mm [THT]"]
  VCC1 = 4 x AAA Battery Mount
  WeMos_D1_Mini1 = WeMos D1 Mini
  R3 = Resistor [tolerance=±5% resistance=510 package=THT]
  R4 = Resistor [tolerance=±5% resistance=1k package=THT]

nets:
  VCC: Part1.VCC, D1.cathode, DHT1.VDD, WeMos_D1_Mini1.5V
  N1: Part1.NC, R3.Pin_0
  N2: Part1.GND, Q1.E, D1.anode
  N3: Q1.B, R4.Pin_0
  N4: DHT1.DATA, WeMos_D1_Mini1.D5
  N5: DHT1.GND, WeMos_D1_Mini1.G
  N6: LED1.cathode, R3.Pin_1
  N7: LED1.anode, VCC1.+
  N8: WeMos_D1_Mini1.D0, R4.Pin_1

custom parts:
  WeMos D1 Mini: The D1 mini is a mini wifi board based on ESP-8266EX.
